# Fritzing sketch BY1 Electrical schematic (saved by Fritzing 0.9.3b)
breadboards: 1

parts:
  SBC1 = Arduino Uno (Rev3)
  LED1 = RGB LED (com. cathode, rgb) [package="5 mm [THT]"]
  R2 = Rotary Potentiometer (Small) [maximum_resistance=100kΩ package=THT]
  D1 = Rectifier Diode [part_number=1N4001 package="300 mil [THT]"]
  R1 = Resistor [tolerance=±5% resistance=220 package=THT]
  T1 = Basic FET P-Channel [package="TO220 [THT]"]
  SRVO1 = Basic Servo
  PS1 = DC Power [voltage=5]
  BLOW1 = DC Motor
  R3 = Resistor [tolerance=±5% resistance=220 package=THT]
  R4 = Resistor [tolerance=±5% resistance=220 package=THT]
  R5 = Resistor [tolerance=±5% resistance=220 package=THT]
  C1 = Electrolytic Capacitor [capacitance=1µF package="100 mil [THT, electrolytic]"]
  S1 = Pushbutton [package=THT]

nets:
  N1: SBC1.A0, R2.wiper
  N2: SBC1.D9_PWM, SRVO1.pulse
  N3: SBC1.D10_PWM/SS, T1.drain
  GND: SBC1.GND, LED1.common_cathode, R2.leg2, R1.Pin_1, T1.source, PS1.V-
  N4: SBC1.D2, S1.leg0
  N5: SBC1.D3_PWM, R3.Pin_0
  N6: SBC1.D4, R4.Pin_0
  N7: SBC1.D5_PWM, R5.Pin_0
  5V: SBC1.5V, R2.leg1
  N8: LED1.red_anode, R3.Pin_1
  N9: LED1.green_anode, R4.Pin_1
  N10: LED1.blue_anode, R5.Pin_1
  N11: D1.cathode, PS1.V+, BLOW1.pin_1
  N12: D1.anode, T1.gate, BLOW1.pin_2
  N13: R1.Pin_0, S1.leg1
  N14: SRVO1.gnd, C1.-
  N15: SRVO1.vcc, C1.+
